// Logisim project Phase (1).circ as structural Verilog: 1 circuit, main circuit main
module main (
  input  Control_1,
  input  A1,
  input  A2,
  input  A3,
  input  A4,
  input  B1,
  input  B2,
  input  Control_0,
  input  B3,
  input  B4
);

  wire n7408_1_p3, n7408_1_p6, n7408_1_p11, n7408_1_p14, n7448_1_p10, n7448_1_p11, n7448_1_p12, n7448_1_p13,
       n7448_1_p14, n7448_1_p15, n7448_1_p16, n7483_1_p2, n7483_1_p6, n7483_1_p10, n7483_1_p15, n74157_1_p3,
       n74157_1_p4, n74157_1_p6, n74157_1_p7, n74157_1_p12, n74157_1_p13, n74157_1_p15, n74157_1_p16,
       n74157_2_p4, n74157_2_p7, n74157_2_p13, n74157_2_p16;

  // _7483 7483_1: pin names not known; wires that end beside it: A4, n7483_1_p2, A3, B3, 1'b1, n7483_1_p6, B2, A2, B4, n7483_1_p10, Control_0, 1'b0, B1, A1, n7483_1_p15
  // _7408 7408_1: pin names not known; wires that end beside it: A1, B1, n7408_1_p3, A2, B2, n7408_1_p6, 1'b0, 1'b1, A3, B3, n7408_1_p11, A4, B4, n7408_1_p14
  // _74157 74157_1: pin names not known; wires that end beside it: Control_0, n7408_1_p3, n74157_1_p3, n74157_1_p4, n7408_1_p6, n74157_1_p6, n74157_1_p7, 1'b0, 1'b1, 1'b0, n7408_1_p11, n74157_1_p12, n74157_1_p13, n7408_1_p14, n74157_1_p15, n74157_1_p16
  // _74157 74157_2: pin names not known; wires that end beside it: Control_1, n74157_1_p4, n7483_1_p15, n74157_2_p4, n74157_1_p7, n7483_1_p6, n74157_2_p7, 1'b0, 1'b1, 1'b0, n74157_1_p13, n7483_1_p2, n74157_2_p13, n74157_1_p16, n7483_1_p10, n74157_2_p16
  // _7432 7432_1: pin names not known; wires that end beside it: A1, B1, n74157_1_p3, A2, B2, n74157_1_p6, 1'b0, 1'b1, A3, B3, n74157_1_p12, A4, B4, n74157_1_p15
  // _7448 7448_1: pin names not known; wires that end beside it: n74157_2_p7, n74157_2_p13, 1'b1, 1'b1, 1'b1, n74157_2_p16, n74157_2_p4, 1'b0, 1'b1, n7448_1_p10, n7448_1_p11, n7448_1_p12, n7448_1_p13, n7448_1_p14, n7448_1_p15, n7448_1_p16
  _7_Segment_Display u_7_segment_display_1 (
    .g(n7448_1_p11), .f(n7448_1_p10), .a(n7448_1_p12), .b(n7448_1_p13), .e(n7448_1_p16), .d(n7448_1_p15),
    .c(n7448_1_p14));  // open: dp
endmodule
