// Logisim project Phase (2).circ as structural Verilog: 1 circuit, main circuit main
module main (
);

  wire clock_1_out, n7448_1_p10, n7448_1_p11, n7448_1_p12, n7448_1_p13, n7448_1_p14, n7448_1_p15,
       n7448_1_p16, n7476_1_p2, n7476_1_p5, n7476_1_p7, n7476_1_p9, n7476_1_p10, n7476_2_p2, n7476_2_p6;

  Clock clock_1 (.out(clock_1_out));
  // _7476 7476_1: pin names not known; wires that end beside it: clock_1_out, n7476_1_p2, 1'b1, clock_1_out, n7476_1_p5, n7476_1_p5, n7476_1_p7, 1'b0, n7476_1_p9, n7476_1_p10
  // _7476 7476_2: pin names not known; wires that end beside it: clock_1_out, n7476_2_p2, 1'b1, n7476_1_p7, n7476_1_p7, n7476_2_p6, 1'b0
  // _7486 7486_1: pin names not known; wires that end beside it: n7476_1_p5, n7476_1_p10, n7476_2_p2, 1'b1, n7476_1_p5, n7476_2_p6, n7476_1_p9
  // _7432 7432_1: pin names not known; wires that end beside it: n7476_2_p6, n7476_1_p10, n7476_1_p2, 1'b1
  // _7448 7448_1: pin names not known; wires that end beside it: n7476_1_p10, n7476_1_p5, 1'b1, 1'b0, 1'b1, 1'b0, n7476_2_p6, 1'b0, 1'b1, n7448_1_p10, n7448_1_p11, n7448_1_p12, n7448_1_p13, n7448_1_p14, n7448_1_p15, n7448_1_p16
  _7_Segment_Display u_7_segment_display_1 (
    .g(n7448_1_p11), .f(n7448_1_p10), .a(n7448_1_p12), .b(n7448_1_p13), .e(n7448_1_p16), .d(n7448_1_p15),
    .c(n7448_1_p14));  // open: dp
endmodule
